// Logisim project Four_Bits_Add_Sub.circ as structural Verilog: 2 circuits, main circuit Add_Sub_4Bits
module Add_Sub_4Bits (
  input  [3:0] A,
  input  [3:0] B,
  input  Add_Sub,
  output [3:0] R,
  output Zero,
  output Overflow
);

  wire add_1bit_1_cout, add_1bit_2_cout, add_1bit_3_cout, add_1bit_4_cout, not_1_out, or_1_out, or_2_out,
       or_3_out, sgn_A_eq_B_out, sgn_A_eq_R_out, sgn_B_eq_R_out, undriven, xnor_1_out, xnor_2_out,
       xnor_3_out, xnor_4_out, xnor_5_out;

  // Probe on A
  xnor xnor_1 (xnor_1_out, B[3], Add_Sub);
  // Probe on B
  xnor xnor_2 (xnor_2_out, B[1], Add_Sub);
  xnor xnor_3 (xnor_3_out, B[2], Add_Sub);
  xnor xnor_4 (xnor_4_out, B[0], Add_Sub);
  Add_1Bit add_1bit_1 (.A(xnor_4_out), .Cout(add_1bit_1_cout), .B(A[0]), .Sum(R[0]));  // open: Cin
  Add_1Bit add_1bit_2 (.A(xnor_2_out), .Cout(add_1bit_2_cout), .B(A[1]), .Sum(R[1]), .Cin(add_1bit_1_cout));
  Add_1Bit add_1bit_3 (.A(xnor_3_out), .Cout(add_1bit_3_cout), .B(A[2]), .Sum(R[2]), .Cin(add_1bit_2_cout));
  Add_1Bit add_1bit_4 (.A(xnor_1_out), .Cout(add_1bit_4_cout), .B(A[3]), .Sum(R[3]), .Cin(add_1bit_3_cout));
  not not_1 (not_1_out, Add_Sub);
  // Probe on R
  or or_1 (or_1_out, R[0], R[1]);
  nor nor_1 (Zero, or_1_out, or_2_out);
  or or_2 (or_2_out, R[2], R[3]);
  xor sgn_B_eq_R (sgn_B_eq_R_out, undriven, R[3]);
  xor sgn_A_eq_R (sgn_A_eq_R_out, A[3], R[3]);
  xnor sgn_A_eq_B (sgn_A_eq_B_out, undriven, A[3]);
  or or_3 (or_3_out, sgn_B_eq_R_out, sgn_A_eq_R_out);
  xnor xnor_5 (xnor_5_out, Add_Sub, sgn_A_eq_B_out);
  and all_sgn_eq (Overflow, xnor_5_out, or_3_out);
  // XOR_Gate xor_1 is placed but not wired

  // Notes on the sheet:
  //   Simon Zheng 260744353
  //   MAKE SURE THAT YOU OPENED THIS PROJECT IN "LOGISIM-EVOLUTION"
  //   YOU CAN FIND "LOGISIM-EVOLUTION" PROGRAM IN THE ASSIGNMENT'S FOLDER
  //   DO NOT USE "LOGISIM" VERSION TO SOLVE THIS ASSIGNMENT!
endmodule

module Add_1Bit (
  input  Cin,
  input  A,
  input  B,
  output Sum,
  output Cout
);

  wire and_1_out, and_2_out, xor_1_out;

  xor xor_1 (xor_1_out, A, B);
  and and_1 (and_1_out, xor_1_out, Cin);
  and and_2 (and_2_out, A, B);
  xor xor_2 (Sum, Cin, xor_1_out);
  or or_1 (Cout, and_1_out, and_2_out);

  // Notes on the sheet:
  //   Simon Zheng 260744353
  //   MAKE SURE THAT YOU OPENED THIS PROJECT IN "LOGISIM-EVOLUTION"
  //   YOU CAN FIND "LOGISIM-EVOLUTION" PROGRAM IN THE ASSIGNMENT'S FOLDER
  //   DO NOT USE "LOGISIM" VERSION TO SOLVE THIS ASSIGNMENT!
endmodule
